// Logisim project 2BIT ASY COUNTER.circ as structural Verilog
module main (
  input  CLK,
  output C,
  output B,
  output A
);

  wire d_ff_1_qn, d_ff_2_qn, d_ff_3_qn, not_1_out;

  not not_1 (not_1_out, CLK);
  D_Flip_Flop d_ff_1 (.clk(not_1_out), .D(d_ff_1_qn), .Q(A), .Qn(d_ff_1_qn));  // open: preset, en, reset
  D_Flip_Flop d_ff_2 (.clk(d_ff_1_qn), .D(d_ff_2_qn), .Q(B), .Qn(d_ff_2_qn));  // open: preset, en, reset
  D_Flip_Flop d_ff_3 (.clk(d_ff_2_qn), .D(d_ff_3_qn), .Q(C), .Qn(d_ff_3_qn));  // open: preset, en, reset

  // Notes on the sheet:
  //   3 BIT ASY. COUNTER
endmodule
