// Logisim project 2bit syn counter.circ as structural Verilog: 1 circuit, main circuit main
module main (
  input  in_1,
  output out_2,
  output out_3
);

  wire d_ff_1_qn, xor_1_out;

  D_Flip_Flop d_ff_1 (.clk(in_1), .D(d_ff_1_qn), .Q(out_3), .Qn(d_ff_1_qn));  // open: preset, en, reset
  D_Flip_Flop d_ff_2 (.clk(in_1), .D(xor_1_out), .Q(out_2));  // open: Qn, preset, en, reset
  xor xor_1 (xor_1_out, out_2, out_3);

  // Notes on the sheet:
  //   2 BIT SYN. COUNTER
endmodule
