// Logisim project 4 bit syn counter.circ as structural Verilog: 1 circuit, main circuit main
module main (
  input  in_1,
  output out_2,
  output out_3,
  output out_4,
  output out_5
);

  wire and_1_out, and_2_out, and_3_out, and_4_out, and_5_out, and_6_out, and_7_out, d_ff_1_qn, d_ff_2_qn,
       d_ff_3_qn, d_ff_4_qn, or_1_out, or_2_out, xor_1_out;

  and and_1 (and_1_out, d_ff_4_qn, out_3, out_2, out_5);
  and and_2 (and_2_out, out_5, d_ff_1_qn);
  and and_3 (and_3_out, out_5, d_ff_2_qn);
  and and_4 (and_4_out, d_ff_3_qn, out_2, out_3);
  and and_5 (and_5_out, out_4, d_ff_3_qn);
  and and_6 (and_6_out, out_4, d_ff_1_qn);
  and and_7 (and_7_out, out_4, d_ff_2_qn);
  xor xor_1 (xor_1_out, out_2, out_3);
  or or_1 (or_1_out, and_2_out, and_3_out, and_4_out);
  or or_2 (or_2_out, and_5_out, and_6_out, and_7_out, and_1_out);
  D_Flip_Flop d_ff_1 (.clk(in_1), .D(d_ff_1_qn), .Q(out_3), .Qn(d_ff_1_qn));  // open: preset, en, reset
  D_Flip_Flop d_ff_2 (.clk(in_1), .D(xor_1_out), .Q(out_2), .Qn(d_ff_2_qn));  // open: preset, en, reset
  D_Flip_Flop d_ff_3 (.clk(in_1), .D(or_1_out), .Q(out_5), .Qn(d_ff_3_qn));  // open: preset, en, reset
  D_Flip_Flop d_ff_4 (.clk(in_1), .D(or_2_out), .Q(out_4), .Qn(d_ff_4_qn));  // open: preset, en, reset

  // Notes on the sheet:
  //   4 bit syn. counter
endmodule
