// Logisim project ALU.circ as structural Verilog: 1 circuit, main circuit main
module main (
);

  Adder adder_1 ();  // open: a, b, out, cin, cout
  Subtractor subtractor_1 ();  // open: a, b, out, bin, bout
  Multiplier multiplier_1 ();  // open: a, b, out, cin, cout
  Divider divider_1 ();  // open: a, b, out, upper, rem
  // XOR_Gate xor_1 is placed but not wired
  // OR_Gate or_1 is placed but not wired
  // AND_Gate and_1 is placed but not wired
endmodule
