// Logisim project Fetch Unit.circ as structural Verilog: 1 circuit, main circuit main
module main (
  input  in_1,
  input  in_2,
  output [31:0] out_3
);

  wire clock_1_out;
  wire [31:0] adder_1_out, register_1_q;

  Clock clock_1 (.out(clock_1_out));
  Register #(.width(32)) register_1 (.D(adder_1_out), .Q(register_1_q), .clk(clock_1_out), .clr(in_1));  // open: en
  Adder #(.width(32)) adder_1 (.a(register_1_q), .b(32'h4), .out(adder_1_out));  // open: cin, cout
  ROM #(.addrWidth(24), .dataWidth(32)) rom_1 (.addr(register_1_q[25:2]), .data(out_3), .sel(in_2));
endmodule
