// Logisim project OR.circ as structural Verilog: 1 circuit, main circuit main
module main (
  input  INPUT_1,
  input  INPUT_2,
  output OUTPUT
);

  wire transistor_4_out;

  Transistor #(.\type ("n")) transistor_1 (.in(1'b1), .out(OUTPUT), .gate(INPUT_1));
  Transistor #(.\type ("n")) transistor_2 (.in(1'b1), .out(OUTPUT), .gate(INPUT_2));
  Transistor transistor_3 (.in(transistor_4_out), .out(OUTPUT), .gate(INPUT_1));
  Transistor transistor_4 (.in(1'b0), .out(transistor_4_out), .gate(INPUT_2));

  // Notes on the sheet:
  //   POWER
  //   GROUND
endmodule
