// Logisim project Register File.circ as structural Verilog: 2 circuits, main circuit main
module main (
  input  Enable,
  input  [31:0] INPUT,
  input  [4:0] in_3,
  input  [4:0] in_4,
  input  in_5,
  input  [4:0] in_6,
  output [31:0] out_7,
  output [31:0] out_8
);

  wire demultiplexer_1_out1, demultiplexer_1_out2, demultiplexer_1_out3, demultiplexer_1_out4,
       demultiplexer_1_out5, demultiplexer_1_out6, demultiplexer_1_out7, demultiplexer_1_out8,
       demultiplexer_1_out9, demultiplexer_1_out10, demultiplexer_1_out11, demultiplexer_1_out12,
       demultiplexer_1_out13, demultiplexer_1_out14, demultiplexer_1_out15, demultiplexer_1_out16,
       demultiplexer_1_out17, demultiplexer_1_out18, demultiplexer_1_out19, demultiplexer_1_out20,
       demultiplexer_1_out21, demultiplexer_1_out22, demultiplexer_1_out23, demultiplexer_1_out24,
       demultiplexer_1_out25, demultiplexer_1_out26, demultiplexer_1_out27, demultiplexer_1_out28,
       demultiplexer_1_out29, demultiplexer_1_out30, demultiplexer_1_out31;
  wire [31:0] register_1_q, register_2_q, register_3_q, register_4_q, register_5_q, register_6_q,
       register_7_q, register_8_q, register_9_q, register_10_q, register_11_q, register_12_q, register_13_q,
       register_14_q, register_15_q, register_16_q, register_17_q, register_18_q, register_19_q,
       register_20_q, register_21_q, register_22_q, register_23_q, register_24_q, register_25_q,
       register_26_q, register_27_q, register_28_q, register_29_q, register_30_q, register_31_q,
       register_32_q;

  Demultiplexer #(.select(5)) demultiplexer_1 (
    .out1(demultiplexer_1_out1), .out2(demultiplexer_1_out2), .out3(demultiplexer_1_out3),
    .out4(demultiplexer_1_out4), .out5(demultiplexer_1_out5), .out6(demultiplexer_1_out6),
    .out7(demultiplexer_1_out7), .out8(demultiplexer_1_out8), .out9(demultiplexer_1_out9),
    .out10(demultiplexer_1_out10), .out11(demultiplexer_1_out11), .out12(demultiplexer_1_out12),
    .out13(demultiplexer_1_out13), .out14(demultiplexer_1_out14), .out15(demultiplexer_1_out15),
    .out16(demultiplexer_1_out16), .out17(demultiplexer_1_out17), .out18(demultiplexer_1_out18),
    .out19(demultiplexer_1_out19), .out20(demultiplexer_1_out20), .out21(demultiplexer_1_out21),
    .out22(demultiplexer_1_out22), .out23(demultiplexer_1_out23), .out24(demultiplexer_1_out24),
    .out25(demultiplexer_1_out25), .out26(demultiplexer_1_out26), .out27(demultiplexer_1_out27),
    .out28(demultiplexer_1_out28), .out29(demultiplexer_1_out29), .out30(demultiplexer_1_out30),
    .out31(demultiplexer_1_out31), .in(Enable), .sel(in_3));  // open: out0, en
  Register #(.width(32)) register_1 (.D(INPUT), .Q(register_1_q), .clk(1'b0), .clr(in_5));  // open: en
  Register #(.width(32)) register_2 (.D(INPUT), .Q(register_2_q), .clk(demultiplexer_1_out4), .clr(in_5));  // open: en
  Register #(.width(32)) register_3 (.D(INPUT), .Q(register_3_q), .clk(demultiplexer_1_out8), .clr(in_5));  // open: en
  Register #(.width(32)) register_4 (.D(INPUT), .Q(register_4_q), .clk(demultiplexer_1_out12), .clr(in_5));  // open: en
  Register #(.width(32)) register_5 (.D(INPUT), .Q(register_5_q), .clk(demultiplexer_1_out16), .clr(in_5));  // open: en
  Register #(.width(32)) register_6 (.D(INPUT), .Q(register_6_q), .clk(demultiplexer_1_out20), .clr(in_5));  // open: en
  Register #(.width(32)) register_7 (.D(INPUT), .Q(register_7_q), .clk(demultiplexer_1_out24), .clr(in_5));  // open: en
  Register #(.width(32)) register_8 (.D(INPUT), .Q(register_8_q), .clk(demultiplexer_1_out28), .clr(in_5));  // open: en
  Register #(.width(32)) register_9 (.D(INPUT), .Q(register_9_q), .clk(demultiplexer_1_out1), .clr(in_5));  // open: en
  Register #(.width(32), .trigger("falling")) register_10 (
    .D(INPUT), .Q(register_10_q), .clk(demultiplexer_1_out5), .clr(in_5));  // open: en
  Register #(.width(32)) register_11 (
    .D(INPUT), .Q(register_11_q), .clk(demultiplexer_1_out9), .clr(in_5));  // open: en
  Register #(.width(32)) register_12 (
    .D(INPUT), .Q(register_12_q), .clk(demultiplexer_1_out13), .clr(in_5));  // open: en
  Register #(.width(32)) register_13 (
    .D(INPUT), .Q(register_13_q), .clk(demultiplexer_1_out17), .clr(in_5));  // open: en
  Register #(.width(32)) register_14 (
    .D(INPUT), .Q(register_14_q), .clk(demultiplexer_1_out21), .clr(in_5));  // open: en
  Register #(.width(32)) register_15 (
    .D(INPUT), .Q(register_15_q), .clk(demultiplexer_1_out25), .clr(in_5));  // open: en
  Register #(.width(32)) register_16 (
    .D(INPUT), .Q(register_16_q), .clk(demultiplexer_1_out29), .clr(in_5));  // open: en
  Register #(.width(32)) register_17 (
    .D(INPUT), .Q(register_17_q), .clk(demultiplexer_1_out2), .clr(in_5));  // open: en
  Register #(.width(32)) register_18 (
    .D(INPUT), .Q(register_18_q), .clk(demultiplexer_1_out6), .clr(in_5));  // open: en
  Register #(.width(32)) register_19 (
    .D(INPUT), .Q(register_19_q), .clk(demultiplexer_1_out10), .clr(in_5));  // open: en
  Register #(.width(32)) register_20 (
    .D(INPUT), .Q(register_20_q), .clk(demultiplexer_1_out14), .clr(in_5));  // open: en
  Register #(.width(32)) register_21 (
    .D(INPUT), .Q(register_21_q), .clk(demultiplexer_1_out18), .clr(in_5));  // open: en
  Register #(.width(32)) register_22 (
    .D(INPUT), .Q(register_22_q), .clk(demultiplexer_1_out22), .clr(in_5));  // open: en
  Register #(.width(32)) register_23 (
    .D(INPUT), .Q(register_23_q), .clk(demultiplexer_1_out26), .clr(in_5));  // open: en
  Register #(.width(32)) register_24 (
    .D(INPUT), .Q(register_24_q), .clk(demultiplexer_1_out30), .clr(in_5));  // open: en
  Register #(.width(32)) register_25 (
    .D(INPUT), .Q(register_25_q), .clk(demultiplexer_1_out3), .clr(in_5));  // open: en
  Register #(.width(32)) register_26 (
    .D(INPUT), .Q(register_26_q), .clk(demultiplexer_1_out7), .clr(in_5));  // open: en
  Register #(.width(32)) register_27 (
    .D(INPUT), .Q(register_27_q), .clk(demultiplexer_1_out11), .clr(in_5));  // open: en
  Register #(.width(32)) register_28 (
    .D(INPUT), .Q(register_28_q), .clk(demultiplexer_1_out15), .clr(in_5));  // open: en
  Register #(.width(32)) register_29 (
    .D(INPUT), .Q(register_29_q), .clk(demultiplexer_1_out19), .clr(in_5));  // open: en
  Register #(.width(32)) register_30 (
    .D(INPUT), .Q(register_30_q), .clk(demultiplexer_1_out23), .clr(in_5));  // open: en
  Register #(.width(32)) register_31 (
    .D(INPUT), .Q(register_31_q), .clk(demultiplexer_1_out27), .clr(in_5));  // open: en
  Register #(.width(32)) register_32 (
    .D(INPUT), .Q(register_32_q), .clk(demultiplexer_1_out31), .clr(in_5));  // open: en
  Multiplexer #(.select(5), .width(32)) multiplexer_1 (
    .in0(register_1_q), .in1(register_9_q), .in2(register_17_q), .in3(register_25_q), .in4(register_2_q),
    .in5(register_10_q), .in6(register_18_q), .in7(register_26_q), .in8(register_3_q), .in9(register_11_q),
    .in10(register_19_q), .in11(register_27_q), .in12(register_4_q), .in13(register_12_q),
    .in14(register_20_q), .in15(register_28_q), .in16(register_5_q), .in17(register_13_q),
    .in18(register_21_q), .in19(register_29_q), .in20(register_6_q), .in21(register_14_q),
    .in22(register_22_q), .in23(register_30_q), .in24(register_7_q), .in25(register_15_q),
    .in26(register_23_q), .in27(register_31_q), .in28(register_8_q), .in29(register_16_q),
    .in30(register_24_q), .in31(register_32_q), .out(out_7), .sel(in_4));  // open: en
  Multiplexer #(.select(5), .width(32)) multiplexer_2 (
    .in0(register_1_q), .in1(register_9_q), .in2(register_17_q), .in3(register_25_q), .in4(register_2_q),
    .in5(register_10_q), .in6(register_18_q), .in7(register_26_q), .in8(register_3_q), .in9(register_11_q),
    .in10(register_19_q), .in11(register_27_q), .in12(register_4_q), .in13(register_12_q),
    .in14(register_20_q), .in15(register_28_q), .in16(register_5_q), .in17(register_13_q),
    .in18(register_21_q), .in19(register_29_q), .in20(register_6_q), .in21(register_14_q),
    .in22(register_22_q), .in23(register_30_q), .in24(register_7_q), .in25(register_15_q),
    .in26(register_23_q), .in27(register_31_q), .in28(register_8_q), .in29(register_16_q),
    .in30(register_24_q), .in31(register_32_q), .out(out_8), .sel(in_6));  // open: en
endmodule

module Final (
  input  in_1,
  input  [31:0] in_2,
  input  [4:0] in_3,
  input  [4:0] in_4,
  input  [4:0] in_5,
  output [31:0] out_6,
  output [31:0] out_7
);

  // main main_1: pin names not known; wires that end beside it: in_1, in_2, in_3, in_4, in_5, out_6, out_7
endmodule
