// Logisim project comparator.circ as structural Verilog: 3 circuits, main circuit main
module main (
  input  in_1,
  input  in_2,
  output A_B,
  output A_B_2,
  output A_B_3
);

  wire not_1_out, not_2_out;

  not not_1 (not_1_out, in_2);
  not not_2 (not_2_out, in_1);
  and and_1 (A_B, in_1, not_1_out);
  xnor xnor_1 (A_B_2, in_1, in_2);
  and and_2 (A_B_3, not_2_out, in_2);
endmodule

module _1_bit_comparator (
  input  A,
  input  B,
  output A_B,
  output A_B_2,
  output A_B_3
);

  main main_1 (.in_1(B), .in_2(A), .A_B(A_B_3), .A_B_2(A_B_2), .A_B_3(A_B));
endmodule

module _1bit_comp_IC (
  input  A0,
  input  B0,
  input  A1,
  input  B1,
  output out_5,
  output out_6,
  output out_7
);

  wire main_1_a_b, main_1_a_b_2, main_1_a_b_3, main_2_a_b, main_2_a_b_2, main_2_a_b_3;

  main main_1 (.in_1(A0), .in_2(B0), .A_B(main_1_a_b), .A_B_2(main_1_a_b_2), .A_B_3(main_1_a_b_3));
  main main_2 (.in_1(A1), .in_2(B1), .A_B(main_2_a_b), .A_B_2(main_2_a_b_2), .A_B_3(main_2_a_b_3));
  and and_1 (out_5, main_2_a_b_3, main_1_a_b_3);
  and and_2 (out_6, main_2_a_b_2, main_1_a_b_2);
  and and_3 (out_7, main_2_a_b, main_1_a_b);
endmodule
