// Logisim project decoder.circ as structural Verilog: 4 circuits, main circuit main
module main (
  input  [31:0] in_1,
  output [6:0] out_2,
  output [4:0] RD,
  output [2:0] F3,
  output [4:0] RS1,
  output [4:0] RS2,
  output [6:0] out_7,
  output [31:0] out_8
);

  wire [2:0] type_1_out_2;
  wire [4:0] demultiplexer_1_out2_2, demultiplexer_1_out5_2;
  wire [11:0] demultiplexer_1_out6;
  wire [20:0] bit_extender_1_out, bit_extender_2_out, bit_extender_3_out, bit_extender_4_out,
       multiplexer_5_out;
  wire [20:1] demultiplexer_1_out6_2;
  wire [24:0] demultiplexer_1_out1;
  wire [31:0] demultiplexer_1_out2, demultiplexer_1_out3, demultiplexer_1_out4, demultiplexer_1_out5;

  \type  type_1 (.in_1(in_1), .out_2(type_1_out_2));  // open: out_3
  Demultiplexer #(.select(3), .width(32)) demultiplexer_1 (
    .out1({out_7, demultiplexer_1_out1}),
    .out2({demultiplexer_1_out2[31:12], demultiplexer_1_out2_2, demultiplexer_1_out2[6:0]}),
    .out3(demultiplexer_1_out3), .out4(demultiplexer_1_out4),
    .out5({demultiplexer_1_out5[31:12], demultiplexer_1_out5_2, demultiplexer_1_out5[6:0]}),
    .out6({demultiplexer_1_out6_2[20], demultiplexer_1_out6_2[8:1], demultiplexer_1_out6_2[9], demultiplexer_1_out6_2[19:10], demultiplexer_1_out6}),
    .in(in_1), .sel(type_1_out_2));  // open: out0, out7, en
  assign bit_extender_1_out = {{9{1'b0}}, {demultiplexer_1_out3[31:25], demultiplexer_1_out3[11:7]}};  // Bit_Extender bit_extender_1
  assign bit_extender_2_out = {{9{1'b0}}, demultiplexer_1_out2[31:20]};  // Bit_Extender bit_extender_2
  assign bit_extender_3_out = {{8{1'b0}}, {demultiplexer_1_out4[31], demultiplexer_1_out4[29:25], demultiplexer_1_out4[11:7], demultiplexer_1_out4[30], 1'b0}};  // Bit_Extender bit_extender_3
  assign bit_extender_4_out = {{1{1'b0}}, demultiplexer_1_out5[31:12]};  // Bit_Extender bit_extender_4
  Multiplexer #(.select(3), .width(5)) multiplexer_1 (
    .in1(demultiplexer_1_out1[11:7]), .in2(demultiplexer_1_out2_2), .in5(demultiplexer_1_out5_2),
    .in6(demultiplexer_1_out6[11:7]), .out(RD), .sel(type_1_out_2));  // open: in0, in3, in4, in7, en
  Multiplexer #(.select(3), .width(3)) multiplexer_2 (
    .in1(demultiplexer_1_out1[14:12]), .in2(demultiplexer_1_out2[14:12]), .in5(demultiplexer_1_out3[14:12]),
    .in6(demultiplexer_1_out4[14:12]), .out(F3), .sel(type_1_out_2));  // open: in0, in3, in4, in7, en
  Multiplexer #(.select(3), .width(5)) multiplexer_3 (
    .in1(demultiplexer_1_out1[19:15]), .in2(demultiplexer_1_out2[19:15]), .in3(demultiplexer_1_out3[19:15]),
    .in4(demultiplexer_1_out4[19:15]), .out(RS1), .sel(type_1_out_2));  // open: in0, in5, in6, in7, en
  Multiplexer #(.select(3), .width(5)) multiplexer_4 (
    .in1(demultiplexer_1_out1[24:20]), .in3(demultiplexer_1_out3[24:20]), .in4(demultiplexer_1_out4[24:20]),
    .out(RS2), .sel(type_1_out_2));  // open: in0, in2, in5, in6, in7, en
  Multiplexer #(.select(3), .width(21)) multiplexer_5 (
    .in2(bit_extender_2_out), .in3(bit_extender_1_out), .in4(bit_extender_3_out), .in5(bit_extender_4_out),
    .in6({demultiplexer_1_out6_2, 1'b0}), .out(multiplexer_5_out), .sel(type_1_out_2));  // open: in0, in1, in7, en
  assign out_8 = {{11{1'b0}}, multiplexer_5_out};  // Bit_Extender bit_extender_5

  assign out_2 = in_1[6:0];

  // Notes on the sheet:
  //   OPCODE
  //   F3
  //   IMMEDIATE
endmodule

module \type  (
  input  [31:0] in_1,
  output [2:0] out_2,
  output out_3
);

  wire comparator_1_eq, comparator_2_eq, comparator_3_eq, comparator_4_eq, comparator_5_eq, comparator_6_eq,
       comparator_7_eq, comparator_9_eq, comparator_10_eq, comparator_11_eq, comparator_12_eq,
       comparator_13_eq, or_1_out, or_2_out, or_3_out;

  Comparator #(.width(7)) comparator_1 (.a(in_1[6:0]), .b(7'b0110011), .eq(comparator_1_eq));  // open: gt, lt
  Comparator #(.width(7)) comparator_2 (.a(in_1[6:0]), .b(7'b0111011), .eq(comparator_2_eq));  // open: gt, lt
  Comparator #(.width(7)) comparator_3 (.a(in_1[6:0]), .b(7'b0010111), .eq(comparator_3_eq));  // open: gt, lt
  Comparator #(.width(7)) comparator_4 (.a(in_1[6:0]), .b(7'b0110111), .eq(comparator_4_eq));  // open: gt, lt
  Comparator #(.width(7)) comparator_5 (.a(in_1[6:0]), .b(7'b1101111), .eq(comparator_5_eq));  // open: gt, lt
  Comparator #(.width(7)) comparator_6 (.a(in_1[6:0]), .b(7'b0100011), .eq(comparator_6_eq));  // open: gt, lt
  Comparator #(.width(7)) comparator_7 (.a(in_1[6:0]), .b(7'b1100011), .eq(comparator_7_eq));  // open: gt, lt
  Comparator #(.width(7)) comparator_8 (.a(in_1[6:0]), .b(7'b0000011), .eq(out_3));  // open: gt, lt
  Comparator #(.width(7)) comparator_9 (.a(in_1[6:0]), .b(7'b0001111), .eq(comparator_9_eq));  // open: gt, lt
  Comparator #(.width(7)) comparator_10 (.a(in_1[6:0]), .b(7'b0010011), .eq(comparator_10_eq));  // open: gt, lt
  Comparator #(.width(7)) comparator_11 (.a(in_1[6:0]), .b(7'b0011011), .eq(comparator_11_eq));  // open: gt, lt
  Comparator #(.width(7)) comparator_12 (.a(in_1[6:0]), .b(7'b1100111), .eq(comparator_12_eq));  // open: gt, lt
  Comparator #(.width(7)) comparator_13 (.a(in_1[6:0]), .b(7'b1110011), .eq(comparator_13_eq));  // open: gt, lt
  or or_1 (or_1_out, comparator_1_eq, comparator_2_eq);
  or or_2 (or_2_out, comparator_3_eq, comparator_4_eq);
  or or_3 (or_3_out, out_3, comparator_9_eq, comparator_10_eq, comparator_11_eq, comparator_12_eq, comparator_13_eq);
  encoder encoder_1 (
    .c(or_1_out), .e(or_3_out), .a(comparator_6_eq), .f(comparator_7_eq), .b(comparator_5_eq), .d(or_2_out),
    .out_7(out_2));

  // Notes on the sheet:
  //   UJ
  //   S
  //   SB
  //   R
  //   U
endmodule

module encoder (
  input  c,
  input  e,
  input  a,
  input  f,
  input  b,
  input  d,
  output [2:0] out_7
);

  wire or_1_out, or_2_out, or_3_out;

  or or_1 (or_1_out, c, b);
  or or_2 (or_2_out, e, d);
  or or_3 (or_3_out, f, d);
  or or_4 (out_7[0], or_1_out, a);
  or or_5 (out_7[1], or_2_out, a);
  or or_6 (out_7[2], or_3_out, b);
endmodule

module \final  (
  input  [31:0] in_1,
  output [6:0] out_2,
  output [4:0] RD,
  output [2:0] F3,
  output [4:0] RS1,
  output [4:0] RS2,
  output [6:0] out_7,
  output [20:0] out_8
);

  wire [31:21] main_1_out_8;

  main main_1 (
    .in_1(in_1), .out_2(out_2), .RD(RD), .F3(F3), .RS1(RS1), .RS2(RS2), .out_7(out_7),
    .out_8({main_1_out_8, out_8}));
  // Pins of 21 and 32 bits meet at {main_1_out_8, out_8}

  // Notes on the sheet:
  //   F7
  //   OPCODE
  //   IMMEDIATE
endmodule
