// Logisim project final.circ as structural Verilog
module CU (
  input  in_1,
  input  in_2,
  input  in_3,
  input  in_4,
  input  in_5,
  input  in_6
);

  wire cu_bro_1_mem_re, cu_bro_1_mem_reg, cu_bro_1_mem_write, cu_bro_1_r2_sel, main_1_p5, main_1_p6,
       main_2_p1, main_2_p6, or_1_out, or_2_out;
  wire [4:0] adder_1_out, main_1_p3, main_1_p4, multiplexer_3_out;
  wire [6:0] main_1_p2;
  wire [6:1] main_1_p7;
  wire [20:0] main_1_p8;
  wire [26:0] adder_1_out_2;
  wire [31:0] adder_2_out, adder_3_out, ALU_p4, bit_extender_1_out, main_2_p7, multiplexer_1_out,
       multiplexer_2_out, multiplexer_4_out, multiplexer_5_out, multiplexer_6_out, ram_1_data, register_1_q,
       rom_1_data, shifter_1_out, shifter_2_out;

  Multiplexer #(.width(32)) multiplexer_1 (
    .in0({adder_1_out_2, adder_1_out}), .in1(adder_3_out), .out(multiplexer_1_out), .sel(in_5));  // open: en
  Multiplexer #(.width(32)) multiplexer_2 (
    .in0(multiplexer_1_out), .in1(ALU_p4), .out(multiplexer_2_out), .sel(in_5));  // open: en
  Register #(.width(32)) register_1 (.D(multiplexer_2_out), .Q(register_1_q), .clk(in_3), .clr(in_6));  // open: en
  Adder #(.width(32)) adder_1 (.a(register_1_q), .b(32'h4), .out({adder_1_out_2, adder_1_out}));  // open: cin, cout
  Shifter #(.width(32)) shifter_1 (.in(bit_extender_1_out), .\dist (5'b01100), .out(shifter_1_out));
  Adder #(.width(32)) adder_2 (.a(register_1_q), .b(shifter_1_out), .out(adder_2_out));  // open: cin, cout
  ROM #(.addrWidth(24), .dataWidth(32)) rom_1 (.addr(register_1_q[25:2]), .data(rom_1_data));  // open: sel
  or or_1 (or_1_out, in_1, in_2);
  Multiplexer #(.width(5)) multiplexer_3 (
    .in0(adder_1_out), .in1(main_1_p3), .out(multiplexer_3_out), .sel(or_1_out));  // open: en
  Shifter #(.width(32)) shifter_2 (.in(bit_extender_1_out), .\dist (5'b00001), .out(shifter_2_out));
  Multiplexer #(.width(32)) multiplexer_4 (
    .in0(ram_1_data), .in1(adder_2_out), .out(multiplexer_4_out), .sel(in_4));  // open: en
  // decoder_main main_1: pin names not known; wires that end beside it: rom_1_data, main_1_p2, main_1_p3, main_1_p4[2:0], main_1_p5, main_1_p6, {main_1_p7, main_1_p4[3]}, main_1_p8
  Adder #(.width(32)) adder_3 (.a(shifter_2_out), .b(register_1_q), .out(adder_3_out));  // open: cin, cout
  Multiplexer #(.width(32)) multiplexer_5 (
    .in0(shifter_1_out), .in1(multiplexer_4_out), .out(multiplexer_5_out));  // open: sel, en
  // Register_File_main main_2: pin names not known; wires that end beside it: main_2_p1, multiplexer_5_out, multiplexer_3_out, main_1_p5, main_1_p6, main_2_p6, main_2_p7
  assign bit_extender_1_out = {{11{1'b0}}, main_1_p8};  // Bit_Extender bit_extender_1
  CU_BRO cu_bro_1 (
    .in_1(main_1_p2), .MEM_WRITE(cu_bro_1_mem_write), .BR(main_1_p4[4]), .MEM_RE(cu_bro_1_mem_re),
    .REG_WR(main_2_p1), .MEM_REG(cu_bro_1_mem_reg), .R2_SEL(cu_bro_1_r2_sel));  // open: ALU_OP, EXTEND_SEL, NXT_PC_SEL
  Multiplexer #(.width(32)) multiplexer_6 (
    .in0(main_2_p7), .in1(bit_extender_1_out), .out(multiplexer_6_out), .sel(cu_bro_1_r2_sel));  // open: en
  // _32_bit_ALU ALU: pin names not known; wires that end beside it: main_2_p6, multiplexer_6_out, main_1_p4, ALU_p4
  or or_2 (or_2_out, cu_bro_1_mem_write, cu_bro_1_mem_re);
  RAM #(.addrWidth(24), .dataWidth(32), .bus("separate")) ram_1 (
    .addr(ALU_p4[23:0]), .din(main_2_p7), .data(ram_1_data), .str(cu_bro_1_mem_write), .sel(or_2_out),
    .clk(in_3), .ld(cu_bro_1_mem_reg));  // open: clr

  // Notes on the sheet:
  //   DECODER
  //   REGISTER FILE
  //   LOAD/STORE
endmodule

module cu_ic (
  input  [6:0] in_1,
  output out_2,
  output out_3,
  output out_4,
  output out_5,
  output out_6,
  output out_7,
  output out_8
);

  wire [2:0] type_1_out_2;
  wire [31:0] bit_extender_1_out;

  assign bit_extender_1_out = {{25{1'b0}}, in_1};  // Bit_Extender bit_extender_1
  \type  type_1 (.in_1(bit_extender_1_out), .out_2(type_1_out_2), .out_3(out_8));
  Demultiplexer #(.select(3)) demultiplexer_1 (
    .out1(out_2), .out2(out_3), .out3(out_4), .out4(out_5), .out5(out_6), .out6(out_7), .in(1'b1),
    .sel(type_1_out_2));  // open: out0, out7, en
endmodule

module CU_BRO (
  input  [6:0] in_1,
  output MEM_WRITE,
  output BR,
  output MEM_RE,
  output REG_WR,
  output MEM_REG,
  output [2:0] ALU_OP,
  output R2_SEL,
  output EXTEND_SEL,
  output NXT_PC_SEL
);

  wire cu_ic_1_out_2, cu_ic_1_out_3;

  cu_ic cu_ic_1 (
    .in_1(in_1), .out_2(cu_ic_1_out_2), .out_3(cu_ic_1_out_3), .out_4(EXTEND_SEL), .out_5(BR), .out_8(MEM_RE));  // open: out_6, out_7
  or or_1 (REG_WR, cu_ic_1_out_2, MEM_RE, cu_ic_1_out_3);
  or or_2 (R2_SEL, MEM_RE, EXTEND_SEL, cu_ic_1_out_3);
  encoder encoder_1 (
    .c(cu_ic_1_out_2), .e(MEM_RE), .a(EXTEND_SEL), .f(cu_ic_1_out_3), .b(BR), .d(1'b0), .out_7(ALU_OP));

  assign MEM_REG = MEM_RE;
  assign MEM_WRITE = EXTEND_SEL;
  assign NXT_PC_SEL = BR;
endmodule
