// Logisim project registors.circ as structural Verilog: 1 circuit, main circuit main
module main (
  input  [31:0] in_1,
  input  [31:0] in_2,
  input  [31:0] in_3,
  input  [4:0] in_4,
  input  [4:0] in_5,
  input  [31:0] in_6,
  input  in_7,
  input  [4:0] in_8
);

  wire [31:0] demultiplexer_1_out1, demultiplexer_1_out2, demultiplexer_1_out3, demultiplexer_1_out4,
       demultiplexer_1_out5, demultiplexer_1_out6, demultiplexer_1_out7, demultiplexer_1_out8,
       demultiplexer_1_out9, demultiplexer_1_out10, demultiplexer_1_out11, demultiplexer_1_out12,
       demultiplexer_1_out13, demultiplexer_1_out14, demultiplexer_1_out15, demultiplexer_1_out16,
       demultiplexer_1_out17, demultiplexer_1_out18, demultiplexer_1_out19, demultiplexer_1_out21,
       demultiplexer_1_out22, demultiplexer_1_out23, demultiplexer_1_out24, demultiplexer_1_out25,
       demultiplexer_1_out26, demultiplexer_1_out27, demultiplexer_1_out28, demultiplexer_1_out29,
       demultiplexer_1_out30, demultiplexer_1_out31, register_1_q, register_2_q, register_3_q, register_4_q,
       register_5_q, register_6_q, register_7_q, register_8_q, register_9_q, register_10_q, register_11_q,
       register_12_q, register_13_q, register_14_q, register_15_q, register_16_q, register_17_q,
       register_18_q, register_19_q, register_20_q, register_21_q, register_22_q, register_23_q,
       register_24_q, register_25_q, register_26_q, register_27_q, register_28_q, register_29_q,
       register_30_q, register_31_q, register_32_q;

  Demultiplexer #(.select(5), .width(32)) demultiplexer_1 (
    .out1(demultiplexer_1_out1), .out2(demultiplexer_1_out2), .out3(demultiplexer_1_out3),
    .out4(demultiplexer_1_out4), .out5(demultiplexer_1_out5), .out6(demultiplexer_1_out6),
    .out7(demultiplexer_1_out7), .out8(demultiplexer_1_out8), .out9(demultiplexer_1_out9),
    .out10(demultiplexer_1_out10), .out11(demultiplexer_1_out11), .out12(demultiplexer_1_out12),
    .out13(demultiplexer_1_out13), .out14(demultiplexer_1_out14), .out15(demultiplexer_1_out15),
    .out16(demultiplexer_1_out16), .out17(demultiplexer_1_out17), .out18(demultiplexer_1_out18),
    .out19(demultiplexer_1_out19), .out20(demultiplexer_1_out16), .out21(demultiplexer_1_out21),
    .out22(demultiplexer_1_out22), .out23(demultiplexer_1_out23), .out24(demultiplexer_1_out24),
    .out25(demultiplexer_1_out25), .out26(demultiplexer_1_out26), .out27(demultiplexer_1_out27),
    .out28(demultiplexer_1_out28), .out29(demultiplexer_1_out29), .out30(demultiplexer_1_out30),
    .out31(demultiplexer_1_out31), .in(in_3), .sel(in_5));  // open: out0, en
  Register #(.width(32)) register_1 (.D(demultiplexer_1_out7), .Q(register_1_q), .clk(in_7));  // open: en, clr
  Register #(.width(32)) register_2 (.D(demultiplexer_1_out15), .Q(register_2_q), .clk(in_7));  // open: en, clr
  Register #(.width(32)) register_3 (.D(demultiplexer_1_out23), .Q(register_3_q), .clk(in_7));  // open: en, clr
  Register #(.width(32)) register_4 (.D(demultiplexer_1_out31), .Q(register_4_q), .clk(in_7));  // open: en, clr
  Register #(.width(32)) register_5 (.D(demultiplexer_1_out6), .Q(register_5_q), .clk(in_7), .clr(in_7));  // open: en
  Register #(.width(32)) register_6 (.D(demultiplexer_1_out14), .Q(register_6_q), .clk(in_7), .clr(in_7));  // open: en
  Register #(.width(32)) register_7 (.D(demultiplexer_1_out22), .Q(register_7_q), .clk(in_7), .clr(in_7));  // open: en
  Register #(.width(32)) register_8 (.D(demultiplexer_1_out30), .Q(register_8_q), .clk(in_7), .clr(in_7));  // open: en
  Register #(.width(32)) register_9 (.D(demultiplexer_1_out5), .Q(register_9_q), .clk(in_7));  // open: en, clr
  Register #(.width(32)) register_10 (.D(demultiplexer_1_out13), .Q(register_10_q), .clk(in_7));  // open: en, clr
  Register #(.width(32)) register_11 (.D(demultiplexer_1_out21), .Q(register_11_q), .clk(in_7));  // open: en, clr
  Register #(.width(32)) register_12 (.D(demultiplexer_1_out29), .Q(register_12_q), .clk(in_7));  // open: en, clr
  Register #(.width(32)) register_13 (.D(demultiplexer_1_out4), .Q(register_13_q), .clk(in_7));  // open: en, clr
  Register #(.width(32)) register_14 (.D(demultiplexer_1_out12), .Q(register_14_q), .clk(in_7));  // open: en, clr
  Register #(.width(32)) register_15 (.D(demultiplexer_1_out16), .Q(register_15_q), .clk(in_7));  // open: en, clr
  Register #(.width(32)) register_16 (.D(demultiplexer_1_out28), .Q(register_16_q), .clk(in_7));  // open: en, clr
  Register #(.width(32)) register_17 (.D(demultiplexer_1_out3), .Q(register_17_q), .clk(in_7));  // open: en, clr
  Register #(.width(32)) register_18 (.D(demultiplexer_1_out11), .Q(register_18_q), .clk(in_7));  // open: en, clr
  Register #(.width(32)) register_19 (.D(demultiplexer_1_out19), .Q(register_19_q), .clk(in_7));  // open: en, clr
  Register #(.width(32)) register_20 (.D(demultiplexer_1_out27), .Q(register_20_q), .clk(in_7));  // open: en, clr
  Register #(.width(32)) register_21 (.D(demultiplexer_1_out2), .Q(register_21_q), .clk(in_7));  // open: en, clr
  Register #(.width(32)) register_22 (.D(demultiplexer_1_out10), .Q(register_22_q), .clk(in_7));  // open: en, clr
  Register #(.width(32)) register_23 (.D(demultiplexer_1_out18), .Q(register_23_q), .clk(in_7));  // open: en, clr
  Register #(.width(32)) register_24 (.D(demultiplexer_1_out26), .Q(register_24_q), .clk(in_7));  // open: en, clr
  Register #(.width(32)) register_25 (.D(demultiplexer_1_out1), .Q(register_25_q), .clk(in_7));  // open: en, clr
  Register #(.width(32)) register_26 (.D(demultiplexer_1_out9), .Q(register_26_q), .clk(in_7));  // open: en, clr
  Register #(.width(32)) register_27 (.D(demultiplexer_1_out17), .Q(register_27_q), .clk(in_7));  // open: en, clr
  Register #(.width(32)) register_28 (.D(demultiplexer_1_out25), .Q(register_28_q), .clk(in_7));  // open: en, clr
  Register #(.width(32)) register_29 (.D(in_1), .Q(register_29_q), .clk(in_7));  // open: en, clr
  Register #(.width(32)) register_30 (.D(demultiplexer_1_out8), .Q(register_30_q), .clk(in_7));  // open: en, clr
  Register #(.width(32)) register_31 (.D(demultiplexer_1_out16), .Q(register_31_q), .clk(in_7));  // open: en, clr
  Register #(.width(32)) register_32 (.D(demultiplexer_1_out24), .Q(register_32_q), .clk(in_7));  // open: en, clr
  Multiplexer #(.select(5), .width(32)) multiplexer_1 (
    .in0(register_1_q), .in1(register_5_q), .in2(register_9_q), .in3(register_13_q), .in4(register_17_q),
    .in5(register_21_q), .in6(register_25_q), .in7(register_29_q), .in8(register_2_q), .in9(register_6_q),
    .in10(register_10_q), .in11(register_14_q), .in12(register_18_q), .in13(register_22_q),
    .in14(register_26_q), .in15(register_30_q), .in16(register_3_q), .in17(register_7_q),
    .in18(register_11_q), .in19(register_15_q), .in20(register_19_q), .in21(register_23_q),
    .in22(register_27_q), .in23(register_31_q), .in24(register_4_q), .in25(register_8_q),
    .in26(register_12_q), .in27(register_16_q), .in28(register_20_q), .in29(register_24_q),
    .in30(register_28_q), .in31(register_32_q), .out(in_2), .sel(in_4));  // open: en
  Multiplexer #(.select(5), .width(32)) multiplexer_2 (
    .in0(register_1_q), .in1(register_5_q), .in2(register_9_q), .in3(register_13_q), .in4(register_17_q),
    .in5(register_21_q), .in6(register_25_q), .in7(register_29_q), .in8(register_2_q), .in9(register_6_q),
    .in10(register_10_q), .in11(register_14_q), .in12(register_18_q), .in13(register_22_q),
    .in14(register_26_q), .in15(register_30_q), .in16(register_3_q), .in17(register_7_q),
    .in18(register_11_q), .in19(register_15_q), .in20(register_19_q), .in21(register_23_q),
    .in22(register_27_q), .in23(register_31_q), .in24(register_4_q), .in25(register_8_q),
    .in26(register_12_q), .in27(register_16_q), .in28(register_20_q), .in29(register_24_q),
    .in30(register_28_q), .in31(register_32_q), .out(in_6), .sel(in_8));  // open: en
endmodule
